# Fritzing sketch Controller (saved by Fritzing 0.9.3b)
breadboards: 1

parts:
  Part1 = Arduino Uno (Rev3)
  Part2 = Bluetooth HC-05 Macho
  Part3 = Thumb Joystick

nets:
  N1: Part1.A3, Part3.HORZ
  N2: Part1.A4/SDA, Part3.VERT
  N3: Part1.D2, Part2.TXD
  N4: Part1.D3_PWM, Part2.RXD
  N5: Part1.D4, Part3.SEL
  VCC: Part1.5V, Part2.VCC, Part3.VCC
  GND: Part1.GND, Part2.GND, Part3.GND
