# Fritzing sketch Hovercraft (saved by Fritzing 0.7.0b)
breadboards: 1

parts:
  Arduino1 = Arduino
  J1 = Basic Servo
  J2 = Basic Servo
  servant_hovercraft = Bluetooth HC-06

nets:
  N1: Arduino1.D5, J2.pulse
  N2: Arduino1.D4, J1.pulse
  N3: Arduino1.D3, servant_hovercraft.RXD
  N4: Arduino1.D2, servant_hovercraft.TXD
  3V3: Arduino1.3V3, servant_hovercraft.VCC
  GND: Arduino1.GND, J1.gnd, J2.gnd, servant_hovercraft.GND

notes:
  HOBBY KING ESC's
